# Fritzing sketch ProyectoFinal (saved by Fritzing 0.9.3b)

parts:
  Componente1 = Arduino Uno (Rev3)
  Componente2 = RFID-RC522-v3
  S1 = H-Bridge with L298N
  J1 = Piezo Speaker
  M1 = Getriebemotor
  M2 = Getriebemotor
  Componente3 = Bluetooth HM-10
  VCC2 = Battery block 9V  # not connected
  Squix1 = OLED 0.96" 128x64 I2C SSD1306
  VCC4 = Battery
  VCC3 = Battery  # not connected
  VCC5 = Battery

nets:
  N1: Componente1.A4/SDA, Squix1.SCA
  N2: Componente1.A5/SCL, Squix1.SCL
  N3: Componente1.D8, S1.IN4
  N4: Componente1.D9_PWM, Componente2.RST
  N5: Componente1.D10_PWM/SS, Componente2.SDA
  N6: Componente1.D11_PWM/MOSI, Componente2.MOSI
  N7: Componente1.D12/MISO, Componente2.MISO
  N8: Componente1.D13/SCK, Componente2.SCK
  GND: Componente1.GND, Componente2.GND, S1.GND, J1.pin1, Componente3.GND, Squix1.GND, VCC5.-
  N9: Componente1.D0/RX, Componente3.TXD
  N10: Componente1.D1/TX, Componente3.RXD
  N11: Componente1.D2, S1.IN1
  N12: Componente1.D3_PWM, J1.pin2
  N13: Componente1.D4, S1.IN2
  N14: Componente1.D5_PWM, S1.ENA
  N15: Componente1.D6_PWM, S1.ENB
  N16: Componente1.D7, S1.IN3
  3V3: Componente1.3V3, Componente2.3.3V
  VCC: Componente1.5V, Componente3.VCC, Squix1.VCC
  N17: S1.12V, VCC4.+
  N18: S1.M1-01, M2.pin_1
  N19: S1.M1-02, M2.pin_2
  N20: S1.M2-01, M1.pin_1
  N21: S1.M2-02, M1.pin_2

custom parts:
  RFID-RC522-v3: A simple China made RFID-RC522 Reader (6x4 cm); do check the pin labels, as this is a MFRC522 based clone.
  H-Bridge with L298N: h-bridge
